// Digital circuit ALU.dig as structural Verilog
module ALU (
  input  [2:0] C,
  input  [7:0] I1,
  input  [7:0] I2,
  output [7:0] O
);

  wire _3bitdecoder_1_p4, add_1_c_o, add_2_c_o, add_3_c_o, add_4_c_o, add_5_c_o, add_6_c_o, add_7_c_o,
       xor_1_out, xor_2_out, xor_3_out, xor_4_out, xor_5_out, xor_6_out, xor_7_out, xor_8_out;
  wire [7:0] _8bitcomparer_1_o, _8bitmultiplier_1_r, add_1_s, and_1_out, bitshifter_1_out, or_1_out,
       xor_9_out;

  // _3bitDecoder _3bitdecoder_1: pin names not known; wires that end beside it: C[0], C[1], C[2], _3bitdecoder_1_p4
  xor xor_1 (xor_1_out, I2[0], _3bitdecoder_1_p4);
  xor xor_2 (xor_2_out, I2[1], _3bitdecoder_1_p4);
  xor xor_3 (xor_3_out, I2[2], _3bitdecoder_1_p4);
  xor xor_4 (xor_4_out, I2[3], _3bitdecoder_1_p4);
  xor xor_5 (xor_5_out, I2[4], _3bitdecoder_1_p4);
  xor xor_6 (xor_6_out, I2[5], _3bitdecoder_1_p4);
  xor xor_7 (xor_7_out, I2[6], _3bitdecoder_1_p4);
  xor xor_8 (xor_8_out, I2[7], _3bitdecoder_1_p4);
  and and_1 (and_1_out[0], I1[0], I2[0]);
  and and_2 (and_1_out[1], I1[1], I2[1]);
  and and_3 (and_1_out[2], I1[2], I2[2]);
  and and_4 (and_1_out[3], I1[3], I2[3]);
  and and_5 (and_1_out[4], I1[4], I2[4]);
  and and_6 (and_1_out[5], I1[5], I2[5]);
  and and_7 (and_1_out[6], I1[6], I2[6]);
  and and_8 (and_1_out[7], I1[7], I2[7]);
  or or_1 (or_1_out[0], I1[0], I2[0]);
  or or_2 (or_1_out[1], I1[1], I2[1]);
  or or_3 (or_1_out[2], I1[2], I2[2]);
  or or_4 (or_1_out[3], I1[3], I2[3]);
  or or_5 (or_1_out[4], I1[4], I2[4]);
  or or_6 (or_1_out[5], I1[5], I2[5]);
  or or_7 (or_1_out[6], I1[6], I2[6]);
  or or_8 (or_1_out[7], I1[7], I2[7]);
  Add add_1 (.a(I1[0]), .b(xor_1_out), .c_i(_3bitdecoder_1_p4), .s(add_1_s[0]), .c_o(add_1_c_o));
  Add add_2 (.a(I1[1]), .b(xor_2_out), .c_i(add_1_c_o), .s(add_1_s[1]), .c_o(add_2_c_o));
  Add add_3 (.a(I1[2]), .b(xor_3_out), .c_i(add_2_c_o), .s(add_1_s[2]), .c_o(add_3_c_o));
  Add add_4 (.a(I1[3]), .b(xor_4_out), .c_i(add_3_c_o), .s(add_1_s[3]), .c_o(add_4_c_o));
  Add add_5 (.a(I1[4]), .b(xor_5_out), .c_i(add_4_c_o), .s(add_1_s[4]), .c_o(add_5_c_o));
  Add add_6 (.a(I1[5]), .b(xor_6_out), .c_i(add_5_c_o), .s(add_1_s[5]), .c_o(add_6_c_o));
  Add add_7 (.a(I1[6]), .b(xor_7_out), .c_i(add_6_c_o), .s(add_1_s[6]), .c_o(add_7_c_o));
  BitShifter bitshifter_1 (.In(I1), .Out(bitshifter_1_out));  // open: Cout
  _8BitMultiplier _8bitmultiplier_1 (.A(I1), .B(I2), .R(_8bitmultiplier_1_r));
  _8BitComparer _8bitcomparer_1 (.A(I1), .B(I2), .O(_8bitcomparer_1_o));
  Add add_8 (.a(I1[7]), .b(xor_8_out), .c_i(add_7_c_o), .s(add_1_s[7]));  // open: c_o
  xor xor_9 (xor_9_out[0], I1[0], I2[0]);
  xor xor_10 (xor_9_out[1], I1[1], I2[1]);
  xor xor_11 (xor_9_out[2], I1[2], I2[2]);
  xor xor_12 (xor_9_out[3], I1[3], I2[3]);
  xor xor_13 (xor_9_out[4], I1[4], I2[4]);
  xor xor_14 (xor_9_out[5], I1[5], I2[5]);
  xor xor_15 (xor_9_out[6], I1[6], I2[6]);
  xor xor_16 (xor_9_out[7], I1[7], I2[7]);
  Multiplexer #(.Selector_Bits(3), .Bits(8)) multiplexer_1 (
    .sel(C), .in_0(add_1_s), .in_1(add_1_s), .in_2(and_1_out), .in_3(or_1_out), .in_4(xor_9_out),
    .in_5(bitshifter_1_out), .in_6(_8bitmultiplier_1_r), .in_7(_8bitcomparer_1_o), .out(O));

  // Notes on the sheet:
  //   0 -> ADD
  //   1 -> SUB
  //   2 -> AND
  //   3 -> OR
  //   4 -> XOR
  //   5 -> SHF
  //   6 -> MUL
  //   7 -> CPR
  //   AND
  //   OR
  //   ADD/SUB
  //   XOR
endmodule
