// Digital circuit 2BitAdder.dig as structural Verilog
module _2BitAdder (
  input  [1:0] A,
  input  [1:0] B,
  input  Cin,
  output [1:0] Sum,
  output Cout
);

  wire adder_1_cout;

  Adder adder_1 (.A(A[0]), .B(B[0]), .Cin(Cin), .Cout(adder_1_cout), .Sum(Sum[0]));
  Adder adder_2 (.A(A[1]), .B(B[1]), .Cin(adder_1_cout), .Cout(Cout), .Sum(Sum[1]));
endmodule
