// Digital circuit 2BitComparer.dig as structural Verilog
module _2BitComparer (
  input  [1:0] A,
  input  [1:0] B,
  input  On,
  output A_lt_B,
  output A_eq_B,
  output A_gt_B
);

  wire comparador_1_a_eq_b, comparador_1_a_gt_b, comparador_1_a_lt_b, comparador_2_a_gt_b,
       comparador_2_a_lt_b;

  comparador comparador_1 (
    .A(A[1]), .B(B[1]), .On(On), .A_eq_B(comparador_1_a_eq_b), .A_gt_B(comparador_1_a_gt_b),
    .A_lt_B(comparador_1_a_lt_b));
  comparador comparador_2 (
    .A(A[0]), .B(B[0]), .On(comparador_1_a_eq_b), .A_eq_B(A_eq_B), .A_gt_B(comparador_2_a_gt_b),
    .A_lt_B(comparador_2_a_lt_b));
  or or_1 (A_lt_B, comparador_1_a_lt_b, comparador_2_a_lt_b);
  or or_2 (A_gt_B, comparador_1_a_gt_b, comparador_2_a_gt_b);
endmodule
