// Digital circuit 3bitDecoder.dig as structural Verilog
module _3bitDecoder (
  input  A2,
  input  A1,
  input  A0,
  output D0,
  output D1,
  output D2,
  output D3,
  output D4,
  output D5,
  output D6,
  output D7
);

  wire and_1_out, and_2_out, and_3_out, and_4_out, and_5_out, and_6_out, and_7_out, and_8_out, not_1_out,
       not_2_out, not_3_out;

  not not_1 (not_1_out, A0);
  not not_2 (not_2_out, A1);
  not not_3 (not_3_out, A2);
  and and_1 (and_1_out, not_1_out, not_2_out);
  and and_2 (and_2_out, A0, not_2_out);
  and and_3 (and_3_out, not_1_out, A1);
  and and_4 (and_4_out, A0, A1);
  and and_5 (and_5_out, not_1_out, not_2_out);
  and and_6 (and_6_out, A0, not_2_out);
  and and_7 (and_7_out, not_1_out, A1);
  and and_8 (and_8_out, A0, A1);
  and and_9 (D0, and_1_out, not_3_out);
  and and_10 (D1, and_2_out, not_3_out);
  and and_11 (D2, and_3_out, not_3_out);
  and and_12 (D3, and_4_out, not_3_out);
  and and_13 (D4, and_5_out, A2);
  and and_14 (D5, and_6_out, A2);
  and and_15 (D6, and_7_out, A2);
  and and_16 (D7, and_8_out, A2);
endmodule
