// Digital circuit 4BitAdder.dig as structural Verilog
module _4BitAdder (
  input  [3:0] A,
  input  [3:0] B,
  input  Cin,
  output Cout,
  output [3:0] Sum
);

  wire _2bitadder_1_cout;

  _2BitAdder _2bitadder_1 (.A(A[1:0]), .B(B[1:0]), .Cin(Cin), .Sum(Sum[1:0]), .Cout(_2bitadder_1_cout));
  _2BitAdder _2bitadder_2 (.A(A[3:2]), .B(B[3:2]), .Cin(_2bitadder_1_cout), .Sum(Sum[3:2]), .Cout(Cout));
endmodule
