// Digital circuit 4BitComparer.dig as structural Verilog
module _4BitComparer (
  input  [3:0] A,
  input  [3:0] B,
  input  On,
  output A_eq_B,
  output A_gt_B,
  output A_lt_B
);

  wire _2bitcomparer_1_a_eq_b, _2bitcomparer_1_a_gt_b, _2bitcomparer_1_a_lt_b, _2bitcomparer_2_a_gt_b,
       _2bitcomparer_2_a_lt_b;

  _2BitComparer _2bitcomparer_1 (
    .A(A[3:2]), .B(B[3:2]), .On(On), .A_lt_B(_2bitcomparer_1_a_lt_b), .A_eq_B(_2bitcomparer_1_a_eq_b),
    .A_gt_B(_2bitcomparer_1_a_gt_b));
  _2BitComparer _2bitcomparer_2 (
    .A(A[1:0]), .B(B[1:0]), .On(_2bitcomparer_1_a_eq_b), .A_lt_B(_2bitcomparer_2_a_lt_b), .A_eq_B(A_eq_B),
    .A_gt_B(_2bitcomparer_2_a_gt_b));
  or or_1 (A_lt_B, _2bitcomparer_1_a_lt_b, _2bitcomparer_2_a_lt_b);
  or or_2 (A_gt_B, _2bitcomparer_1_a_gt_b, _2bitcomparer_2_a_gt_b);
endmodule
