// Digital circuit 4BitMultiplicationPartialStep.dig as structural Verilog
module _4BitMultiplicationPartialStep (
  input  A,
  input  [3:0] B,
  output [3:0] R
);

  and and_1 (R[0], A, B[0]);
  and and_2 (R[1], A, B[1]);
  and and_3 (R[2], A, B[2]);
  and and_4 (R[3], A, B[3]);
endmodule
