// Digital circuit 4BitMultiplier.dig as structural Verilog
module _4BitMultiplier (
  input  [1:0] A,
  input  [1:0] B,
  output [3:0] R
);

  wire [1:0] _2bitmultiplicationpartialstep_1_r, _2bitmultiplicationpartialstep_2_r;
  wire [3:0] _4bitshifter_1_r;

  _2BitMultiplicationPartialStep _2bitmultiplicationpartialstep_1 (
    .A(A[0]), .B(B), .R(_2bitmultiplicationpartialstep_1_r));
  _2BitMultiplicationPartialStep _2bitmultiplicationpartialstep_2 (
    .A(A[1]), .B(B), .R(_2bitmultiplicationpartialstep_2_r));
  _4BitShifter _4bitshifter_1 (
    .A({2'b00, _2bitmultiplicationpartialstep_2_r}), .Cin(1'b0), .R(_4bitshifter_1_r));  // open: Cout
  _4BitAdder _4bitadder_1 (
    .A(_4bitshifter_1_r), .B({2'b00, _2bitmultiplicationpartialstep_1_r}), .Cin(1'b0), .Sum(R));  // open: Cout
endmodule
