// Digital circuit 4BitShifter.dig as structural Verilog
module _4BitShifter (
  input  [3:0] A,
  input  Cin,
  output [3:0] R,
  output Cout
);


  assign Cout = A[3];
  assign R = {A[2:0], Cin};
endmodule
