// Digital circuit 8BitAdder.dig as structural Verilog
module _8BitAdder (
  input  [7:0] A,
  input  [7:0] B,
  input  Cin,
  output [7:0] Sum,
  output Cout
);

  wire _4bitadder_1_cout;

  _4BitAdder _4bitadder_1 (.A(A[3:0]), .B(B[3:0]), .Cin(Cin), .Cout(_4bitadder_1_cout), .Sum(Sum[3:0]));
  _4BitAdder _4bitadder_2 (.A(A[7:4]), .B(B[7:4]), .Cin(_4bitadder_1_cout), .Cout(Cout), .Sum(Sum[7:4]));
endmodule
