// Digital circuit 8BitComparer.dig as structural Verilog
module _8BitComparer (
  input  [7:0] A,
  input  [7:0] B,
  output [7:0] O
);

  wire _4bitcomparer_1_a_eq_b, _4bitcomparer_1_a_gt_b, _4bitcomparer_1_a_lt_b, _4bitcomparer_2_a_gt_b,
       _4bitcomparer_2_a_lt_b;

  _4BitComparer _4bitcomparer_1 (
    .A(A[7:4]), .B(B[7:4]), .On(1'b1), .A_eq_B(_4bitcomparer_1_a_eq_b), .A_gt_B(_4bitcomparer_1_a_gt_b),
    .A_lt_B(_4bitcomparer_1_a_lt_b));
  _4BitComparer _4bitcomparer_2 (
    .A(A[3:0]), .B(B[3:0]), .On(_4bitcomparer_1_a_eq_b), .A_eq_B(O[0]), .A_gt_B(_4bitcomparer_2_a_gt_b),
    .A_lt_B(_4bitcomparer_2_a_lt_b));
  or or_1 (O[1], _4bitcomparer_2_a_gt_b, _4bitcomparer_1_a_gt_b);
  or or_2 (O[2], _4bitcomparer_2_a_lt_b, _4bitcomparer_1_a_lt_b);

  assign O[7:3] = {5{1'b0}};
endmodule
