// Digital circuit 8BitMultiplier.dig as structural Verilog
module _8BitMultiplier (
  input  [7:0] A,
  input  [7:0] B,
  output [7:0] R
);

  wire _8bitadder_1_cout, _8bitadder_2_cout;
  wire [3:0] _4bitmultiplier_1_r, _4bitmultiplier_2_r, _4bitmultiplier_3_r, _4bitmultiplier_4_r;
  wire [7:0] _8bitadder_1_sum, _8bitadder_2_sum, bitshifter_1_out, bitshifter_2_out, bitshifter_3_out,
       bitshifter_4_out, bitshifter_5_out, bitshifter_6_out, bitshifter_7_out, bitshifter_8_out;

  _4BitMultiplier _4bitmultiplier_1 (.A(A[1:0]), .B(B[1:0]), .R(_4bitmultiplier_1_r));
  _4BitMultiplier _4bitmultiplier_2 (.A(A[1:0]), .B(B[3:2]), .R(_4bitmultiplier_2_r));
  _4BitMultiplier _4bitmultiplier_3 (.A(A[3:2]), .B(B[1:0]), .R(_4bitmultiplier_3_r));
  BitShifter bitshifter_1 (.In({4'b0000, _4bitmultiplier_2_r}), .Out(bitshifter_1_out));  // open: Cout
  _4BitMultiplier _4bitmultiplier_4 (.A(A[3:2]), .B(B[3:2]), .R(_4bitmultiplier_4_r));
  BitShifter bitshifter_2 (.In(bitshifter_1_out), .Out(bitshifter_2_out));  // open: Cout
  BitShifter bitshifter_3 (.In({4'b0000, _4bitmultiplier_3_r}), .Out(bitshifter_3_out));  // open: Cout
  BitShifter bitshifter_4 (.In({4'b0000, _4bitmultiplier_4_r}), .Out(bitshifter_4_out));  // open: Cout
  _8BitAdder _8bitadder_1 (
    .A({4'b0000, _4bitmultiplier_1_r}), .B(bitshifter_2_out), .Cin(1'b0), .Sum(_8bitadder_1_sum),
    .Cout(_8bitadder_1_cout));
  BitShifter bitshifter_5 (.In(bitshifter_3_out), .Out(bitshifter_5_out));  // open: Cout
  BitShifter bitshifter_6 (.In(bitshifter_4_out), .Out(bitshifter_6_out));  // open: Cout
  BitShifter bitshifter_7 (.In(bitshifter_6_out), .Out(bitshifter_7_out));  // open: Cout
  _8BitAdder _8bitadder_2 (
    .A(_8bitadder_1_sum), .B(bitshifter_5_out), .Cin(_8bitadder_1_cout), .Sum(_8bitadder_2_sum),
    .Cout(_8bitadder_2_cout));
  BitShifter bitshifter_8 (.In(bitshifter_7_out), .Out(bitshifter_8_out));  // open: Cout
  _8BitAdder _8bitadder_3 (.A(_8bitadder_2_sum), .B(bitshifter_8_out), .Cin(_8bitadder_2_cout), .Sum(R));  // open: Cout
  // also tied to GND on the sheet: {A[4], A[5], A[6], A[7], B[4], B[5], B[6], B[7]}
endmodule
