// Digital circuit 8bit-register.dig as structural Verilog
module _8bit_register (
  input  [7:0] I,
  input  W,
  input  R,
  output [7:0] O
);

  wire [7:0] d_ff_1_q;

  D_FF d_ff_1 (.D(I[0]), .C(W), .Q(d_ff_1_q[0]));  // open: nQ
  D_FF d_ff_2 (.D(I[1]), .C(W), .Q(d_ff_1_q[1]));  // open: nQ
  D_FF d_ff_3 (.D(I[2]), .C(W), .Q(d_ff_1_q[2]));  // open: nQ
  D_FF d_ff_4 (.D(I[3]), .C(W), .Q(d_ff_1_q[3]));  // open: nQ
  D_FF d_ff_5 (.D(I[4]), .C(W), .Q(d_ff_1_q[4]));  // open: nQ
  D_FF d_ff_6 (.D(I[5]), .C(W), .Q(d_ff_1_q[5]));  // open: nQ
  D_FF d_ff_7 (.D(I[6]), .C(W), .Q(d_ff_1_q[6]));  // open: nQ
  D_FF d_ff_8 (.D(I[7]), .C(W), .Q(d_ff_1_q[7]));  // open: nQ
  Multiplexer #(.Bits(8)) multiplexer_1 (.sel(R), .in_0({8{1'b0}}), .in_1(d_ff_1_q), .out(O));

  // Notes on the sheet:
  //   I: 8bit input
  //   W: Write enable
  //   R: Read enable
  //   O: 8bit output
endmodule
