// Digital circuit Adder.dig as structural Verilog
module Adder (
  input  A,
  input  B,
  input  Cin,
  output Cout,
  output Sum
);

  wire half_adder_1_cout, half_adder_1_sum, half_adder_2_cout;

  Half_Adder half_adder_1 (.A(A), .B(B), .Sum(half_adder_1_sum), .Cout(half_adder_1_cout));
  Half_Adder half_adder_2 (.A(Cin), .B(half_adder_1_sum), .Sum(Sum), .Cout(half_adder_2_cout));
  or or_1 (Cout, half_adder_2_cout, half_adder_1_cout);
endmodule
