// Digital circuit comparador.dig as structural Verilog
module comparador (
  input  A,
  input  B,
  input  On,
  output A_eq_B,
  output A_gt_B,
  output A_lt_B
);

  wire not_1_out, not_2_out, xnor_1_out;

  not not_1 (not_1_out, B);
  not not_2 (not_2_out, A);
  xnor xnor_1 (xnor_1_out, A, B);
  and and_1 (A_gt_B, A, not_1_out, On);
  and and_2 (A_lt_B, not_2_out, B, On);
  and and_3 (A_eq_B, xnor_1_out, On);
endmodule
