// Digital circuit main.dig as structural Verilog
module main (
  input  [2:0] in_1,
  input  [7:0] Input_1,
  input  [7:0] Input_2
);

  wire CLK_out;
  wire [3:0] _8bit_register_1_o;
  wire [7:0] alu_1_o;
  wire [7:4] _8bit_register_1_o_2;

  ALU alu_1 (.C(in_1), .I1(Input_1), .I2(Input_2), .O(alu_1_o));
  Button CLK (.out(CLK_out));
  _8bit_register _8bit_register_1 (.I(alu_1_o), .W(CLK_out), .R(1'b1), .O({_8bit_register_1_o_2, _8bit_register_1_o}));
  Seven_Seg_Hex seven_seg_hex_1 (.d(_8bit_register_1_o_2), .dp(1'b0));
  Seven_Seg_Hex seven_seg_hex_2 (.d(_8bit_register_1_o), .dp(1'b0));

  // Notes on the sheet:
  //   Opcode (3bit)
  //   0 -> ADD
  //   1 -> SUB
  //   2 -> AND
  //   3 -> OR
  //   4 -> XOR
  //   5 -> SHIFT
  //   6 -> MULT
  //   7 -> COMP
  //   Com opcode COMP (7 - comparação):
  //   01: A = B
  //   02: A > B
  //   04: A < B
endmodule
